# Fritzing sketch Force (saved by Fritzing 1.0.2b)

parts:
  Bauteil1 = HX711 Weighing Sensor Module
  Load_Cell1 = Load Cell - Red/white/black/green
  MCU1 = Wemos Lolin32lite
  U1 = LIPO-110mAh [package=lipo-110]
  S1 = Toggle Switch [package=THT]
  S2 = Pushbutton [package="[SMD]"]

nets:
  N1: Bauteil1.VCC, MCU1.pin_28
  N2: Bauteil1.GND, MCU1.pin_13
  N3: Bauteil1.DO/RX, MCU1.pin_20
  N4: Bauteil1.CK/TX, MCU1.pin_23
  N5: Bauteil1.E+, Load_Cell1.wire1
  N6: Bauteil1.E-, Load_Cell1.wire3
  N7: Bauteil1.A+, Load_Cell1.wire2
  N8: Bauteil1.A-, Load_Cell1.wire4
  N9: MCU1.pin_14, S1.L2
  N10: MCU1.pin_18, S2.Pin_3, S2.Pin_4
  N11: U1.+, S1.COM

custom parts:
  Load Cell - Red/white/black/green: A rectangle load cell/weighting pressure Sensor with four wires - Red, white, black, green. Normally corresponding with E+, E-, A+, A- respectively.
  Wemos Lolin32lite: Wemos Lolinlite32 wifi and blue tooth board based on the ESP-32 cpu, digital I/Os 19, analog inputs 6, clock 240mhz, Flash 4Mbytes, lipo battery charger (500ma connection broken out on breadboard but not pcb), usb.
