# Fritzing sketch LightGate (saved by Fritzing 1.0.2b)

parts:
  MCU1 = Wemos Lolin32lite
  Enc1 = shaft encoder
  BAT1 = Battery Holders [package=lipo-1100mAh]
  S1 = SPST Switch [package=switch-spdt_kit]
  U1 = RJ45 Jack [package=rj45-8]
  U2 = RJ45 Jack [package=rj45-8]
  Enc2 = shaft encoder
  LED1 = LED - 5mm [color="Red (633nm)" current=0.030A package="5 mm [THT]"]

nets:
  N1: MCU1.pin_8, U1.6
  N2: MCU1.pin_13, Enc1.GND, LED1.cathode
  N3: MCU1.pin_14, S1.P
  N4: MCU1.pin_15, BAT1.-
  N5: MCU1.pin_16, LED1.anode
  N6: MCU1.pin_21, U1.3
  N7: MCU1.pin_22, Enc1.OUT
  N8: MCU1.pin_28, Enc1.VCC, U1.2
  N9: BAT1.+, S1.O
  N10: U2.2, Enc2.VCC
  N11: U2.3, Enc2.OUT
  N12: U2.6, U2.7, Enc2.GND

custom parts:
  Wemos Lolin32lite: Wemos Lolinlite32 wifi and blue tooth board based on the ESP-32 cpu, digital I/Os 19, analog inputs 6, clock 240mhz, Flash 4Mbytes, lipo battery charger (500ma connection broken out on breadboard but not pcb), usb.
