# Fritzing sketch LightGate_single (saved by Fritzing 0.9.6b)

parts:
  part = Wemos Lolin32lite
  Lichtschranke = shaft encoder
  Schalter = SPST Switch [package=switch-spdt_kit]
  LED = LED - 5mm [color="Red (633nm)" current=0.030A package="5 mm [THT]"]
  LiPo-Batterie = LIPO-110mAh [package=lipo-110]

nets:
  N1: part.pin_13, Lichtschranke.GND, LED.cathode
  N2: part.pin_14, Schalter.P
  N3: part.pin_15, LiPo-Batterie.-
  N4: part.pin_16, LED.anode
  N5: part.pin_22, Lichtschranke.OUT
  N6: part.pin_28, Lichtschranke.VCC
  N7: Schalter.O, LiPo-Batterie.+

custom parts:
  Wemos Lolin32lite: Wemos Lolinlite32 wifi and blue tooth board based on the ESP-32 cpu, digital I/Os 19, analog inputs 6, clock 240mhz, Flash 4Mbytes, lipo battery charger (500ma connection broken out on breadboard but not pcb), usb.
